// Digital circuit CPU.dig as structural Verilog
module CPU (
  input  clock
);

  wire and_1_out, and_2_out, branch_unit_p3, execution_unit_zero, not_1_out, or_1_out, pc_incrementer_p4;
  wire [1:0] reg_file_p3;
  wire [11:0] MainControl_d;
  wire [15:0] bitextender_1_out, execution_unit_r, instructionReg_d, multiplexer_1_out, multiplexer_2_out,
       programCounter_q, ramdualport_1_d, reg_file_p4, reg_file_p7, reg_file_p8, shift_left_1_1_out;

  D_FF #(.Bits(16)) programCounter (.D(multiplexer_1_out), .C(~clock), .Q(programCounter_q));  // open: nQ
  // ALU pc_incrementer: pin names not known; wires that end beside it: programCounter_q, 16'h2, 4'b0010, pc_incrementer_p4
  ROM #(.AddrBits(16), .Bits(16)) instructionReg (.A(programCounter_q), .sel(1'b1), .D(instructionReg_d));
  Multiplexer multiplexer_1 (
    .sel(or_1_out), .in_0(pc_incrementer_p4), .in_1(branch_unit_p3), .out(multiplexer_1_out[0]));
  ROM #(.AddrBits(4), .Bits(12)) MainControl (.A(instructionReg_d[15:12]), .sel(1'b1), .D(MainControl_d));
  // reg_file reg_file: pin names not known; wires that end beside it: instructionReg_d[11:10], instructionReg_d[9:8], reg_file_p3, reg_file_p4, MainControl_d[8], clock, reg_file_p7, reg_file_p8
  BitExtender bitextender_1 (.in(instructionReg_d[7:0]), .out(bitextender_1_out));
  shift_left_1 shift_left_1_1 (.in(bitextender_1_out), .out(shift_left_1_1_out));
  // ALU branch_unit: pin names not known; wires that end beside it: pc_incrementer_p4, shift_left_1_1_out, branch_unit_p3
  Multiplexer #(.Bits(16)) multiplexer_2 (
    .sel(MainControl_d[10]), .in_0(reg_file_p8), .in_1(bitextender_1_out), .out(multiplexer_2_out));
  Multiplexer #(.Bits(2)) multiplexer_3 (
    .sel(MainControl_d[11]), .in_0(instructionReg_d[9:8]), .in_1(instructionReg_d[7:6]), .out(reg_file_p3));
  ALU execution_unit (
    .zero(execution_unit_zero), .r(execution_unit_r), .a(reg_file_p7), .b(multiplexer_2_out),
    .s(MainControl_d[3:0]));  // open: overflow
  and and_1 (and_1_out, MainControl_d[6], execution_unit_zero);
  not not_1 (not_1_out, execution_unit_zero);
  and and_2 (and_2_out, MainControl_d[5], not_1_out);
  RAMDualPort ramdualport_1 (
    .A(execution_unit_r[1:0]), .Din(reg_file_p8[0]), .str(MainControl_d[7]), .C(clock),
    .ld(MainControl_d[9]), .D(ramdualport_1_d[0]));
  or or_1 (or_1_out, and_1_out, and_2_out);
  Multiplexer #(.Bits(16)) multiplexer_4 (
    .sel(MainControl_d[4]), .in_0(execution_unit_r), .in_1(ramdualport_1_d), .out(reg_file_p4));
  // Pins of 1 and 16 bits meet at reg_file_p8
  // Pins of 1 and 16 bits meet at multiplexer_1_out
  // Pins of 2 and 16 bits meet at execution_unit_r
  // Pins of 1 and 16 bits meet at ramdualport_1_d

  // Notes on the sheet:
  //   IF/ID
  //   contents of MainControl (hex, n*v repeats v):
  //   52,56,50,51,5c,5d,57,32
  //   TODO bit
  //   ordering
  //   RegDest
  //   ALUsrc
  //   MemToReg
  //   RegWrite
  //   MemWrite
  //   Branch
  //   BNE
  //   ALUOp
  //   ID/EX
  //   EX/MA
  //   BranchTaken
  //   PCSrc
  //   BNETaken
  //   MA/WB
endmodule
